# Fritzing sketch tamrin1 (saved by Fritzing 0.9.4)
breadboards: 1

parts:
  Part1 = Arduino Uno (Rev3) - ICSP  # not connected
  R1 = Rotary Potentiometer (Large) [maximum_resistance=100kΩ package=THT]
  LCD1 = LCD screen

nets:
  VSS: R1.leg1, R1.leg2, LCD1.VSS, LCD1.VDD, LCD1.R/W, LCD1.LED+, LCD1.LED-
  N1: R1.wiper, LCD1.V0
