# Fritzing sketch tamrin4 (saved by Fritzing 0.9.4)
breadboards: 1

parts:
  Part1 = Arduino Uno (Rev3)
  hc-sr1 = hc-sr04
  LED1 = LED - 3mm [color="Red (633nm)" package="3 mm [THT]"]

nets:
  N1: Part1.D11_PWM/MOSI, hc-sr1.Trig
  N2: Part1.D12/MISO, hc-sr1.Echo
  N3: Part1.D3_PWM, LED1.anode
  5V: Part1.5V, hc-sr1.VCC
  GND: Part1.GND, hc-sr1.GND, LED1.cathode
